# Fritzing sketch shrek_esp32 (saved by Fritzing 0.9.5d)
breadboards: 1

parts:
  R1 = TRIMPOT [package=3386u]
  OLED_I2C1 = OLED 128x64 I2C Monochrome Display
  M1 = DOIT Esp32 DevKit v1 (30 pins long, 11 pins width) [part_number=ESP32S-PIN30]

nets:
  N1: R1.CCW, M1.VIN
  N2: R1.WIPER, M1.D15
  GND: R1.CW, OLED_I2C1.GND, M1.GND
  N3: OLED_I2C1.SDA, M1.D21
  N4: OLED_I2C1.SCK, M1.D22
  VDD: OLED_I2C1.VDD, M1.3V3

custom parts:
  DOIT Esp32 DevKit v1 (30 pins long, 11 pins width): The DOIT Esp32 DevKit v1 is one of the development board created by DOIT to evaluate the ESP-WROOM-32 module. It is based on the ESP32 microcontroller that boasts Wifi, Bluetooth, Ethernet and Low Power support all in a single chip. (vanepp) made breadboard work, adjusted pin numbering and labels and reduced size of schematic and cleaned up pcb. This chip is 30pins long (2 x15) and 11 pins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
